# Fritzing sketch Encoder dynamic test (saved by Fritzing 0.9.9b)

parts:
  Bauteil1 = Arduino Uno (Rev3)
  Bauteil2 = Arduino Uno (Rev3)

nets:
  N1: Bauteil1.A4/SDA, Bauteil2.A4/SDA
  N2: Bauteil1.A5/SCL, Bauteil2.A5/SCL
  N3: Bauteil1.D2, Bauteil2.D2
  N4: Bauteil1.D3_PWM, Bauteil2.D3_PWM
  N5: Bauteil1.D4, Bauteil2.D4
  GND: Bauteil1.GND, Bauteil2.GND
