# Fritzing sketch Encoder static test (saved by Fritzing 0.9.9b)

parts:
  Bauteil1 = Arduino Uno (Rev3)
  Bauteil2 = Arduino Uno (Rev3)
  RE2 = KY-040 Rotary encoder [package="Breakout board"]

nets:
  N1: Bauteil1.A4/SDA, Bauteil2.A4/SDA
  N2: Bauteil1.A5/SCL, Bauteil2.A5/SCL
  GND: Bauteil1.GND, Bauteil2.GND, RE2.GND
  N3: Bauteil2.D2, RE2.CLK
  N4: Bauteil2.D3_PWM, RE2.DT
  N5: Bauteil2.D4, RE2.SW
  5V: Bauteil2.5V, RE2.Vcc

custom parts:
  KY-040 Rotary encoder: KY-040 Rotary Encoder with switch on breakout borad from AZ Delivery
